// Digital circuit Dividendo.dig as structural Verilog
module Dividendo (
  input  [3:0] Reminder_A,
  input  [3:0] Divisor_M,
  input  [3:0] Dividendo_Q,
  output [3:0] A1,
  output [3:0] Q1
);

  wire c;
  wire [3:0] sub_1_s;

  not not_1 (Q1[0], c);
  Sub #(.Bits(4)) sub_1 (.a({Reminder_A[2:0], Dividendo_Q[3]}), .b(Divisor_M), .c_i(1'b0), .s(sub_1_s), .c_o(c));
  Multiplexer #(.Bits(4)) multiplexer_1 (.sel(c), .in_0(sub_1_s), .in_1({Reminder_A[2:0], Dividendo_Q[3]}), .out(A1));

  assign Q1[3:1] = Dividendo_Q[2:0];

  // Other names for the same wires on the sheet: q[3:1] = Dividendo_Q[2:0]; s_0 = Dividendo_Q[0];
  //   s_1 = Dividendo_Q[1]; s_2 = Dividendo_Q[2]; s_3 = Dividendo_Q[3]; sa[3:0] = {Reminder_A[2:0], Dividendo_Q[3]};
  //   m[3:0] = Divisor_M; s_4 = Reminder_A[0]; s_5 = Reminder_A[1]; s_6 = Reminder_A[2]; s_7 = Reminder_A[3]
endmodule
