// Digital circuit Divisor.dig as structural Verilog
module Divisor (
  input  [3:0] Divisor,
  input  [3:0] Dividendo,
  output [3:0] remainder,
  output [3:0] quotient
);

  wire xor_1_out;
  wire [3:0] a_1, a_2, add_1_s, add_2_s, add_3_s, add_4_s, dividendo_1_a1, dividendo_1_q1, dividendo_2_a1,
       dividendo_2_q1, dividendo_3_a1, dividendo_3_q1, m_1, not_1_out, not_2_out, not_3_out, not_4_out, q_1;

  assign not_1_out = ~Dividendo;  // Not not_1, 4 bits wide
  assign not_2_out = ~Divisor;  // Not not_2, 4 bits wide
  Add #(.Bits(4)) add_1 (.a(not_1_out), .b(4'b0001), .c_i(1'b0), .s(add_1_s));  // open: c_o
  Add #(.Bits(4)) add_2 (.a(not_2_out), .b(4'b0001), .c_i(1'b0), .s(add_2_s));  // open: c_o
  Dividendo dividendo_1 (
    .Reminder_A(4'b0000), .Divisor_M(m_1), .Dividendo_Q(a_1), .A1(dividendo_1_a1), .Q1(dividendo_1_q1));
  Multiplexer #(.Bits(4)) multiplexer_1 (.sel(Dividendo[3]), .in_0(Dividendo), .in_1(add_1_s), .out(a_1));
  Multiplexer #(.Bits(4)) multiplexer_2 (.sel(Divisor[3]), .in_0(Divisor), .in_1(add_2_s), .out(m_1));
  Dividendo dividendo_2 (
    .Reminder_A(dividendo_1_a1), .Divisor_M(m_1), .Dividendo_Q(dividendo_1_q1), .A1(dividendo_2_a1),
    .Q1(dividendo_2_q1));
  Dividendo dividendo_3 (
    .Reminder_A(dividendo_2_a1), .Divisor_M(m_1), .Dividendo_Q(dividendo_2_q1), .A1(dividendo_3_a1),
    .Q1(dividendo_3_q1));
  assign not_3_out = ~q_1;  // Not not_3, 4 bits wide
  assign not_4_out = ~a_2;  // Not not_4, 4 bits wide
  Add #(.Bits(4)) add_3 (.a(not_3_out), .b(4'b0001), .c_i(1'b0), .s(add_3_s));  // open: c_o
  xor xor_1 (xor_1_out, Dividendo[3], Divisor[3]);
  Add #(.Bits(4)) add_4 (.a(not_4_out), .b(4'b0001), .c_i(1'b0), .s(add_4_s));  // open: c_o
  Dividendo dividendo_4 (
    .Reminder_A(dividendo_3_a1), .Divisor_M(m_1), .Dividendo_Q(dividendo_3_q1), .A1(a_2), .Q1(q_1));
  Multiplexer #(.Bits(4)) multiplexer_3 (.sel(xor_1_out), .in_0(q_1), .in_1(add_3_s), .out(quotient));
  Multiplexer #(.Bits(4)) multiplexer_4 (.sel(Dividendo[3]), .in_0(a_2), .in_1(add_4_s), .out(remainder));

  // Other names for the same wires on the sheet: a[3:0] = Dividendo; s_a = Dividendo[3]; m[3:0] = Divisor;
  //   s_m = Divisor[3]
endmodule

/* Test case:
Dividendo Divisor quotient remainder
loop(a, 7)
	loop(b, 7)
let nA = a * -1;
let nB = (b+1) * -1;




(a) (b+1) (a/(b+1)) (a%(b+1))
(a) (nB) (a/nB) (a%nB)
(nA) (b+1) (nA/(b+1)) (nA%(b+1))
(nA) (nB) (nA/nB) (nA%nB) 

	end loop
end loop
*/
