// Digital circuit memdecoder.dig as structural Verilog
module memdecoder (
  input  Enable,
  input  [31:0] VirtualAddres,
  output [10:0] Physical_Addres,
  output Invalid_Addres
);

  wire comparator_3_lt, comparator_4_gt, GlobalMemory, or_2_out, Stack;
  wire [31:0] add_1_s, multiplexer_1_out, multiplexer_2_out, multiplexer_3_out, multiplexer_4_out,
       multiplexer_5_out, or_1_out, sub_1_s;

  Comparator #(.Bits(4)) comparator_1 (.a(VirtualAddres[31:28]), .b(4'b0001), .eq(GlobalMemory));  // open: gt, lt
  Comparator #(.Bits(4)) comparator_2 (.a(VirtualAddres[31:28]), .b(4'b0111), .eq(Stack));  // open: gt, lt
  Multiplexer #(.Bits(32)) multiplexer_1 (
    .sel(Stack), .in_0(32'h10000000), .in_1(32'h7fffebfc), .out(multiplexer_1_out));
  Sub #(.Bits(32)) sub_1 (.a(VirtualAddres), .b(multiplexer_1_out), .c_i(1'b0), .s(sub_1_s));  // open: c_o
  Add #(.Bits(32)) add_1 (.a(sub_1_s), .b(32'h400), .c_i(1'b0), .s(add_1_s));  // open: c_o
  Multiplexer #(.Bits(32)) multiplexer_2 (
    .sel(Stack), .in_0(32'h100003ff), .in_1(32'h7fffeffb), .out(multiplexer_2_out));
  Multiplexer #(.Bits(32)) multiplexer_3 (
    .sel(Stack), .in_0(32'h10000000), .in_1(32'h7fffebfc), .out(multiplexer_3_out));
  Multiplexer #(.Bits(32)) multiplexer_4 (
    .sel(GlobalMemory), .in_0({32{1'b0}}), .in_1(sub_1_s), .out(multiplexer_4_out));
  Multiplexer #(.Bits(32)) multiplexer_5 (.sel(Stack), .in_0({32{1'b0}}), .in_1(add_1_s), .out(multiplexer_5_out));
  Comparator #(.Bits(32)) comparator_3 (
    .a(VirtualAddres), .b(multiplexer_3_out), .lt(comparator_3_lt));  // open: gt, eq
  Comparator #(.Bits(32)) comparator_4 (
    .a(VirtualAddres), .b(multiplexer_2_out), .gt(comparator_4_gt));  // open: eq, lt
  assign or_1_out = multiplexer_4_out | multiplexer_5_out;  // Or or_1, 32 bits wide
  or or_2 (or_2_out, comparator_3_lt, comparator_4_gt);
  Multiplexer #(.Bits(11)) multiplexer_6 (
    .sel(Invalid_Addres), .in_0(or_1_out[10:0]), .in_1({11{1'b0}}), .out(Physical_Addres));
  Multiplexer multiplexer_7 (.sel(Enable), .in_0(1'b0), .in_1(or_2_out), .out(Invalid_Addres));

  // Other names for the same wires on the sheet: VirtualA[31:0] = VirtualAddres
endmodule

/* Test case:
Enable	        VirtualAddres	Physical_Addres Invalid_Addres
1		0x10000000	0		0
1		0x100003FF	1023		0
1		0x10000138	312		0
1		0x10873487	0		1
1		0x7FFFEBFC	1024		0
1		0x7FFFEFFB	2047		0
1		0x7FFFEEF9	1789		0
1		0x8FFFB45A	0		1
1		0x7FFFEFFC      0               1
0		0x7FFFEFFC      0               1
*/
